// Digital circuit 2022.dig as structural Verilog
module _2022 (
  input  [7:0] A,
  input  Add,
  input  Reset,
  input  in_4,
  output [3:0] out_5
);

  wire comparator_1_eq, or_1_out;
  wire [3:0] add_1_s, add_1_s_2, counter_1_out, counter_2_out, mul_1_mul;
  wire [7:4] mul_1_mul_2;
  wire [11:8] add_1_s_3;

  or or_1 (or_1_out, Add, Reset);
  Counter #(.Bits(4)) counter_1 (.en(1'b1), .C(or_1_out), .clr(Reset), .out(counter_1_out));  // open: ovf
  Add #(.Bits(12)) add_1 (
    .a({4'b0000, A}), .b({{8{1'b0}}, counter_1_out}), .c_i(1'b0), .s({add_1_s_3, add_1_s_2, add_1_s}));  // open: c_o
  Counter #(.Bits(4)) counter_2 (.en(1'b1), .C(in_4), .clr(comparator_1_eq), .out(counter_2_out));  // open: ovf
  Comparator #(.Bits(4)) comparator_1 (.a(counter_2_out), .b(4'b0100), .eq(comparator_1_eq));  // open: gt, lt
  Seven_Seg_Hex seven_seg_hex_1 (.d(add_1_s_3), .dp(1'b0));
  Mul #(.Bits(4)) mul_1 (.a(counter_2_out), .b(4'b0011), .mul({mul_1_mul_2, mul_1_mul}));
  Seven_Seg_Hex seven_seg_hex_2 (.d(add_1_s_2), .dp(1'b0));
  Seven_Seg_Hex seven_seg_hex_3 (.d(add_1_s), .dp(1'b0));
  Seven_Seg_Hex seven_seg_hex_4 (.d(out_5), .dp(1'b0));
  Add #(.Bits(4)) add_2 (.a(mul_1_mul), .b(4'b0011), .c_i(1'b0), .s(out_5));  // open: c_o
endmodule
