// Digital circuit 02.dig as structural Verilog
module _02 (
  input  A,
  input  B,
  output And,
  output Or,
  output Nand,
  output Nor,
  output Xor,
  output Xnor
);

  or or_1 (Or, A, B);
  nor nor_1 (Nor, A, B);
  xnor xnor_1 (Xnor, A, B);
  and and_1 (And, A, B);
  nand nand_1 (Nand, A, B);
  xor xor_1 (Xor, A, B);
endmodule
