// Digital circuit 05.dig as structural Verilog
module _05 (
  input  A,
  input  B,
  input  C,
  input  D,
  output Z4,
  output Z5,
  output Z6,
  output Z1,
  output Z3,
  output Z2
);

  wire and_1_out, and_2_out, and_3_out, and_4_out, and_5_out, and_6_out, and_7_out, and_8_out, not_1_out,
       not_2_out, not_3_out, not_4_out, not_5_out, not_6_out, not_7_out, not_8_out, not_9_out, not_10_out,
       not_11_out, not_12_out, not_13_out, not_14_out, not_15_out, not_16_out, not_17_out, not_18_out,
       not_19_out, not_20_out, not_21_out, not_22_out, not_23_out, not_24_out, or_1_out, or_2_out, or_3_out,
       or_4_out, or_5_out, or_6_out, or_7_out, or_8_out, or_9_out, or_10_out, or_11_out, or_12_out;

  and and_1 (and_1_out, A, not_1_out);
  not not_1 (not_1_out, C);
  and and_2 (and_2_out, B, not_2_out, not_3_out);
  not not_2 (not_2_out, C);
  not not_3 (not_3_out, D);
  and and_3 (and_3_out, A, B, not_4_out);
  not not_4 (not_4_out, D);
  and and_4 (and_4_out, C, not_5_out);
  not not_5 (not_5_out, A);
  and and_5 (and_5_out, not_6_out, C, D);
  not not_6 (not_6_out, B);
  and and_6 (and_6_out, not_7_out, not_8_out, D);
  not not_7 (not_7_out, A);
  not not_8 (not_8_out, B);
  and and_7 (and_7_out, not_9_out, not_10_out);
  not not_9 (not_9_out, Z4);
  not not_10 (not_10_out, Z5);
  and and_8 (and_8_out, Z4, Z5);
  not not_11 (not_11_out, C);
  not not_12 (not_12_out, D);
  not not_13 (not_13_out, A);
  not not_14 (not_14_out, C);
  not not_15 (not_15_out, B);
  not not_16 (not_16_out, C);
  not not_17 (not_17_out, D);
  not not_18 (not_18_out, A);
  not not_19 (not_19_out, B);
  not not_20 (not_20_out, B);
  not not_21 (not_21_out, A);
  not not_22 (not_22_out, A);
  not not_23 (not_23_out, Z2);
  not not_24 (not_24_out, Z1);
  or or_1 (or_1_out, not_11_out, not_12_out);
  or or_2 (or_2_out, A, B);
  or or_3 (or_3_out, not_13_out, B, not_14_out);
  or or_4 (or_4_out, not_15_out, A, not_16_out);
  or or_5 (or_5_out, C, A, not_17_out);
  or or_6 (or_6_out, not_18_out, not_19_out);
  or or_7 (or_7_out, C, D);
  or or_8 (or_8_out, A, not_20_out, C);
  or or_9 (or_9_out, B, not_21_out, C);
  or or_10 (or_10_out, B, not_22_out, D);
  or or_11 (or_11_out, Z1, not_23_out);
  or or_12 (or_12_out, not_24_out, Z2);
  or or_13 (Z4, and_1_out, and_2_out, and_3_out);
  or or_14 (Z5, and_4_out, and_5_out, and_6_out);
  or or_15 (Z6, and_7_out, and_8_out);
  and and_9 (Z1, or_1_out, or_2_out, or_3_out, or_4_out, or_5_out);
  and and_10 (Z2, or_6_out, or_7_out, or_8_out, or_9_out, or_10_out);
  and and_11 (Z3, or_11_out, or_12_out);
endmodule
