// Digital circuit 09.dig as structural Verilog
module _09 (
  input  X0,
  input  X1,
  input  S1,
  input  X2,
  input  X3,
  input  S0,
  output Z
);

  wire and_1_out, and_2_out, and_3_out, and_4_out, and_5_out, and_6_out, and_7_out, and_8_out, not_1_out,
       not_2_out, not_3_out, not_4_out;

  and and_1 (and_1_out, not_1_out, not_2_out);
  not not_1 (not_1_out, S1);
  not not_2 (not_2_out, S0);
  and and_2 (and_2_out, S1, not_3_out);
  not not_3 (not_3_out, S0);
  and and_3 (and_3_out, S0, not_4_out);
  not not_4 (not_4_out, S1);
  and and_4 (and_4_out, S1, S0);
  and and_5 (and_5_out, X0, and_1_out);
  and and_6 (and_6_out, X1, and_2_out);
  and and_7 (and_7_out, X2, and_3_out);
  and and_8 (and_8_out, X3, and_4_out);
  or or_1 (Z, and_5_out, and_6_out, and_7_out, and_8_out);

  // Other names for the same wires on the sheet: S0_t = S1; S1_t = S0
endmodule
