// Digital circuit 01.dig as structural Verilog
module _01 (
  input  [3:0] In,
  output a,
  output b,
  output c,
  output d,
  output e,
  output f,
  output g
);

  wire and_1_out, and_2_out, and_3_out, and_4_out, and_5_out, and_6_out, and_7_out, and_8_out, and_9_out,
       and_10_out, and_11_out, and_12_out, and_13_out, and_14_out, not_1_out, not_2_out, not_3_out;

  not not_1 (not_1_out, In[2]);
  not not_2 (not_2_out, In[1]);
  not not_3 (not_3_out, In[0]);
  and and_1 (and_1_out, not_1_out, not_3_out);
  and and_2 (and_2_out, In[2], In[0]);
  and and_3 (and_3_out, not_2_out, not_3_out);
  and and_4 (and_4_out, In[1], In[0]);
  or or_1 (c, In[2], not_2_out, In[0]);
  and and_5 (and_5_out, not_1_out, not_3_out);
  and and_6 (and_6_out, not_1_out, In[1]);
  and and_7 (and_7_out, In[2], not_2_out, In[0]);
  and and_8 (and_8_out, In[1], not_3_out);
  and and_9 (and_9_out, not_1_out, not_3_out);
  and and_10 (and_10_out, In[1], not_3_out);
  and and_11 (and_11_out, not_2_out, not_3_out);
  and and_12 (and_12_out, not_1_out, In[1]);
  and and_13 (and_13_out, In[2], not_2_out);
  and and_14 (and_14_out, In[1], not_3_out);
  or or_2 (a, In[3], and_1_out, and_2_out, In[1]);
  or or_3 (b, not_1_out, and_3_out, and_4_out);
  or or_4 (d, In[3], and_5_out, and_6_out, and_7_out, and_8_out);
  or or_5 (e, and_9_out, and_10_out);
  or or_6 (f, In[3], In[2], and_11_out);
  or or_7 (g, In[3], and_12_out, and_13_out, and_14_out);
  Seven_Seg seven_seg_1 (.a(a), .b(b), .c(c), .d(d), .e(e), .f(f), .g(g), .dp(1'b0));

  // Other names for the same wires on the sheet: D_t = In[0]; C_t = In[1]; B_t = In[2]; A_t = In[3]
endmodule
