// Digital circuit 02.dig as structural Verilog
module _02 (
  input  clk,
  input  [2:0] In,
  output [7:0] Z
);

  wire and_1_out, and_2_out, and_3_out, and_4_out, and_5_out, and_6_out, and_7_out, and_8_out, and_9_out,
       and_10_out, and_11_out, and_12_out, and_13_out, and_14_out, and_15_out, not_1_out, not_2_out,
       not_3_out;

  not not_1 (not_1_out, In[2]);
  not not_2 (not_2_out, In[1]);
  not not_3 (not_3_out, In[0]);
  and and_1 (and_1_out, In[0], not_2_out, not_1_out);
  and and_2 (and_2_out, not_3_out, In[1]);
  and and_3 (and_3_out, not_3_out, In[2]);
  and and_4 (and_4_out, In[1], In[2]);
  and and_5 (and_5_out, In[0], not_1_out);
  and and_6 (and_6_out, not_2_out, In[2]);
  and and_7 (and_7_out, not_3_out, not_2_out);
  and and_8 (and_8_out, In[1], not_1_out);
  and and_9 (and_9_out, not_2_out, In[2]);
  and and_10 (and_10_out, not_3_out, In[1], not_1_out);
  and and_11 (and_11_out, not_3_out, not_2_out, In[2]);
  and and_12 (and_12_out, In[0], In[1], In[2]);
  and and_13 (and_13_out, In[0], not_2_out, not_1_out);
  and and_14 (and_14_out, not_3_out, In[1]);
  and and_15 (and_15_out, not_3_out, In[2]);
  or or_1 (Z[5], and_1_out, and_2_out, and_3_out, and_4_out);
  or or_2 (Z[3], and_5_out, and_6_out);
  or or_3 (Z[2], and_7_out, and_8_out, and_9_out);
  or or_4 (Z[1], and_10_out, and_11_out, and_12_out);
  or or_5 (Z[0], and_13_out, and_14_out, and_15_out);
  Terminal terminal_1 (.D({2'b01, Z[5], 1'b0, Z[3:0]}), .C(clk), .en(1'b1));

  assign {Z[7:6], Z[4]} = 3'b010;

  // Other names for the same wires on the sheet: In_0 = In[0]; In_1 = In[1]; In_2 = In[2]; Z_0 = Z[0]; Z_1 = Z[1];
  //   Z_2 = Z[2]; Z_3 = Z[3]; Z_5 = Z[5]
endmodule
