// Digital circuit 02.dig as structural Verilog
module _02 (
  input  [6:0] In,
  output [6:0] Output
);

  wire blocka_1_c1, blocka_1_c2, blocka_1_c3;
  wire [6:0] blockb_1_out;

  BlockA blocka_1 (.In(In), .C1(blocka_1_c1), .C2(blocka_1_c2), .C3(blocka_1_c3));
  BlockB blockb_1 (.C1(blocka_1_c1), .C2(blocka_1_c2), .C3(blocka_1_c3), .Out(blockb_1_out));
  BlockC blockc_1 (.In1(blockb_1_out), .In2(In), .Output(Output));
endmodule
