// Digital circuit BlockB.dig as structural Verilog
module BlockB (
  input  C1,
  input  C2,
  input  C3,
  output [6:0] Out
);

  wire not_1_out, not_2_out, not_3_out;

  not not_1 (not_1_out, C1);
  not not_2 (not_2_out, C2);
  not not_3 (not_3_out, C3);
  and and_1 (Out[0], not_1_out, not_2_out, C3);
  and and_2 (Out[1], not_1_out, C2, not_3_out);
  and and_3 (Out[2], not_1_out, C2, C3);
  and and_4 (Out[3], C1, not_2_out, not_3_out);
  and and_5 (Out[4], C1, not_2_out, C3);
  and and_6 (Out[5], C1, C2, not_3_out);
  and and_7 (Out[6], C1, C2, C3);
  // Pins of 1 and 7 bits meet at Out
endmodule
