// Digital circuit BlockC.dig as structural Verilog
module BlockC (
  input  [6:0] In1,
  input  [6:0] In2,
  output [6:0] Output
);

  xor xor_1 (Output[0], In1[0], In2[0]);
  xor xor_2 (Output[1], In1[1], In2[1]);
  xor xor_3 (Output[2], In1[2], In2[2]);
  xor xor_4 (Output[3], In1[3], In2[3]);
  xor xor_5 (Output[4], In1[4], In2[4]);
  xor xor_6 (Output[5], In1[5], In2[5]);
  xor xor_7 (Output[6], In1[6], In2[6]);
endmodule
