// Digital circuit 04.dig as structural Verilog
module _04 (
  input  [3:0] In,
  output [3:0] Output
);

  wire not_2_out;
  wire [2:0] add_1_s, not_1_out;

  assign not_1_out = ~In[2:0];  // Not not_1, 3 bits wide
  Add #(.Bits(3)) add_1 (.a(not_1_out), .b(3'b001), .c_i(1'b0), .s(add_1_s));  // open: c_o
  Multiplexer #(.Bits(4)) multiplexer_1 (.sel(not_2_out), .in_0({In[3], add_1_s}), .in_1(In), .out(Output));
  not not_2 (not_2_out, In[3]);
endmodule
