// Digital circuit 01.dig as structural Verilog
module _01 (
  input  [3:0] A,
  input  [3:0] B,
  input  [2:0] S,
  input  M,
  input  C,
  output [3:0] F,
  output Cout
);

  wire arithmetic_1_cout;
  wire [3:0] arithmetic_1_sum, logical_1_out;

  Logical logical_1 (.A(A), .B(B), .S(S), .Out(logical_1_out));
  Arithmetic arithmetic_1 (.A(A), .B(B), .S(S), .Cin(C), .Sum(arithmetic_1_sum), .Cout(arithmetic_1_cout));
  Multiplexer #(.Bits(4)) multiplexer_1 (.sel(M), .in_0(logical_1_out), .in_1(arithmetic_1_sum), .out(F));
  Multiplexer multiplexer_2 (.sel(M), .in_0(1'b0), .in_1(arithmetic_1_cout), .out(Cout));
endmodule
