// Digital circuit Adder.dig as structural Verilog
module Adder (
  input  [3:0] A,
  input  [3:0] B,
  input  Cin,
  input  Mode,
  output Cout,
  output [7:0] F
);

  wire add_2_c_o, add_3_c_o, add_4_c_o;
  wire [3:0] flipper_1_out, multiplexer_1_out;

  Flipper flipper_1 (.In(B), .Out(flipper_1_out));  // open: Enable
  Multiplexer #(.Bits(4)) multiplexer_1 (.sel(Mode), .in_0(B), .in_1(flipper_1_out), .out(multiplexer_1_out));
  Add add_1 (.a(A[0]), .b(multiplexer_1_out[0]), .c_i(add_2_c_o), .s(F[0]), .c_o(Cout));
  Add add_2 (.a(A[1]), .b(multiplexer_1_out[1]), .c_i(add_3_c_o), .s(F[1]), .c_o(add_2_c_o));
  Add add_3 (.a(A[2]), .b(multiplexer_1_out[2]), .c_i(add_4_c_o), .s(F[2]), .c_o(add_3_c_o));
  Add add_4 (.a(A[3]), .b(multiplexer_1_out[3]), .c_i(Cin), .s(F[3]), .c_o(add_4_c_o));
  // Pins of 4 and 8 bits meet at F
endmodule
