// Digital circuit Arithmetic.dig as structural Verilog
module Arithmetic (
  input  [3:0] A,
  input  [3:0] B,
  input  [2:0] S,
  input  Cin,
  output [3:0] Sum,
  output Cout
);

  wire add_2_c_o, lshift_1_cout, multiplexer_2_out, rshift_1_cout, Shift;
  wire [1:0] Enable_out, Mode_out;
  wire [3:0] add_1_s, add_2_s, flipper_1_out, flipper_2_out, lshift_1_out, Minus_out, multiplexer_1_out,
       multiplexer_3_out, multiplexer_4_out, rshift_1_out;

  and and_1 (Shift, S[2], S[1]);
  LookUpTable #(.Bits(2)) Enable (.in0(S[0]), .in1(S[1]), .in2(S[2]), .out(Enable_out));
  LookUpTable #(.Bits(2)) Mode (.in0(S[0]), .in1(S[1]), .in2(S[2]), .out(Mode_out));
  LShift lshift_1 (.In(A), .Out(lshift_1_out), .Cout(lshift_1_cout));
  RShift rshift_1 (.In(A), .Out(rshift_1_out), .Cout(rshift_1_cout));
  Multiplexer #(.Bits(4)) multiplexer_1 (.sel(Enable_out[0]), .in_0(4'b0000), .in_1(A), .out(multiplexer_1_out));
  Multiplexer multiplexer_2 (.sel(S[0]), .in_0(lshift_1_cout), .in_1(rshift_1_cout), .out(multiplexer_2_out));
  Multiplexer #(.Bits(4)) multiplexer_3 (.sel(Enable_out[1]), .in_0(4'b0000), .in_1(B), .out(multiplexer_3_out));
  Multiplexer #(.Bits(4)) multiplexer_4 (.sel(S[0]), .in_0(lshift_1_out), .in_1(rshift_1_out), .out(multiplexer_4_out));
  Flipper flipper_1 (.In(multiplexer_1_out), .Enable(Mode_out[0]), .Out(flipper_1_out));
  Flipper flipper_2 (.In(multiplexer_3_out), .Enable(Mode_out[1]), .Out(flipper_2_out));
  LookUpTable #(.Bits(4)) Minus (.in0(S[0]), .in1(S[1]), .in2(S[2]), .out(Minus_out));
  Add #(.Bits(4)) add_1 (.a(flipper_1_out), .b(flipper_2_out), .c_i(1'b0), .s(add_1_s));  // open: c_o
  Add #(.Bits(4)) add_2 (.a(add_1_s), .b(Minus_out), .c_i(Cin), .s(add_2_s), .c_o(add_2_c_o));
  Multiplexer #(.Bits(4)) multiplexer_5 (.sel(Shift), .in_0(add_2_s), .in_1(multiplexer_4_out), .out(Sum));
  Multiplexer multiplexer_6 (.sel(Shift), .in_0(add_2_c_o), .in_1(multiplexer_2_out), .out(Cout));

  // Other names for the same wires on the sheet: L_R = S[0]

  // Notes on the sheet:
  //   contents of Enable (hex, n*v repeats v):
  //   1,1,3,3,1,2
  //   contents of Mode (hex, n*v repeats v):
  //   0,0,0,16,1
  //   contents of Minus (hex, n*v repeats v):
  //   0,ffffffffffffffff,0,f,f
endmodule
