// Digital circuit Flipper.dig as structural Verilog
module Flipper (
  input  [3:0] In,
  input  Enable,
  output [3:0] Out
);

  wire not_2_out;
  wire [3:0] add_1_s, not_1_out;

  assign not_1_out = ~In;  // Not not_1, 4 bits wide
  Add #(.Bits(4)) add_1 (.a(not_1_out), .b(4'b0001), .c_i(1'b0), .s(add_1_s));  // open: c_o
  Multiplexer #(.Bits(4)) multiplexer_1 (.sel(not_2_out), .in_0(add_1_s), .in_1(In), .out(Out));
  not not_2 (not_2_out, Enable);
endmodule
