// Digital circuit Logical.dig as structural Verilog
module Logical (
  input  [3:0] A,
  input  [3:0] B,
  input  [2:0] S,
  output [3:0] Out
);

  wire [3:0] and_1_out, and_2_out, and_3_out, and_4_out, multiplexer_1_out, multiplexer_2_out,
       multiplexer_3_out, not_1_out, not_2_out, not_3_out, or_1_out, or_2_out;

  assign not_1_out = ~B;  // Not not_1, 4 bits wide
  assign not_2_out = ~A;  // Not not_2, 4 bits wide
  assign and_1_out = A & B;  // And and_1, 4 bits wide
  assign or_1_out = A | B;  // Or or_1, 4 bits wide
  assign and_2_out = A & not_1_out;  // And and_2, 4 bits wide
  assign and_3_out = not_2_out & B;  // And and_3, 4 bits wide
  Multiplexer #(.Bits(4)) multiplexer_1 (.sel(S[2]), .in_0(4'b1111), .in_1(4'b0000), .out(multiplexer_1_out));
  assign and_4_out = and_3_out & multiplexer_1_out;  // And and_4, 4 bits wide
  assign or_2_out = and_2_out | and_4_out;  // Or or_2, 4 bits wide
  Multiplexer #(.Bits(4), .Selector_Bits(2)) multiplexer_2 (
    .sel(S[1:0]), .in_0(A), .in_1(and_1_out), .in_2(or_1_out), .in_3(or_2_out), .out(multiplexer_2_out));
  Multiplexer #(.Selector_Bits(2), .Bits(4)) multiplexer_3 (
    .sel(S[1:0]), .in_0(and_1_out), .in_1(or_1_out), .in_2(or_2_out), .in_3(A), .out(multiplexer_3_out));
  assign not_3_out = ~multiplexer_2_out;  // Not not_3, 4 bits wide
  Multiplexer #(.Bits(4)) multiplexer_4 (.sel(S[2]), .in_0(not_3_out), .in_1(multiplexer_3_out), .out(Out));
endmodule
