// Digital circuit 03.dig as structural Verilog
module _03 (
  input  J,
  input  K,
  input  Clear,
  input  Clock,
  output Q,
  output Q_2
);

  wire and_1_out, and_2_out, and_3_out, and_4_out, not_1_out, or_1_out, or_2_out, rs_ff_as_1_nq, rs_ff_as_1_q;

  and and_1 (and_1_out, J, Clock, Q_2);
  and and_2 (and_2_out, Q, K, Clock);
  or or_1 (or_1_out, and_2_out, Clear);
  RS_FF_AS rs_ff_as_1 (.S(and_1_out), .R(or_1_out), .Q(rs_ff_as_1_q), .nQ(rs_ff_as_1_nq));
  not not_1 (not_1_out, Clock);
  and and_3 (and_3_out, not_1_out, rs_ff_as_1_q);
  and and_4 (and_4_out, not_1_out, rs_ff_as_1_nq);
  or or_2 (or_2_out, and_4_out, Clear);
  RS_FF_AS rs_ff_as_2 (.S(and_3_out), .R(or_2_out), .Q(Q), .nQ(Q_2));
endmodule
