// Digital circuit 05.dig as structural Verilog
module _05 (
  input  T,
  input  Clock,
  input  Clear,
  output Q,
  output Q_2
);

  wire and_1_out, and_2_out;

  and and_1 (and_1_out, T, Clock, Q);
  and and_2 (and_2_out, Q_2, Clock, T);
  nor nor_1 (Q, and_1_out, Q_2);
  nor nor_2 (Q_2, Q, and_2_out);
endmodule
