// Digital circuit 01- b.dig as structural Verilog
module _01__b (
  input  Clock,
  input  P,
  input  T,
  input  D,
  input  C,
  input  B,
  input  A,
  input  Clr,
  input  Load,
  output QD,
  output QC,
  output QB,
  output QA,
  output RCO
);

  wire and_1_out, and_2_out, and_3_out, and_4_out, and_5_out, and_6_out, and_7_out, and_8_out, and_9_out,
       and_10_out, and_11_out, and_12_out, and_13_out, and_14_out, and_15_out, and_16_out, and_17_out,
       and_18_out, and_19_out, and_20_out, nand_1_out, not_1_out, not_2_out, not_3_out, not_4_out, not_5_out,
       not_6_out, or_1_out, or_2_out, or_3_out, or_4_out;

  and and_1 (and_1_out, Load, QD);
  not not_1 (not_1_out, and_1_out);
  and and_2 (and_2_out, Load, QC);
  not not_2 (not_2_out, and_2_out);
  and and_3 (and_3_out, Load, QB);
  not not_3 (not_3_out, and_3_out);
  not not_4 (not_4_out, and_4_out);
  and and_4 (and_4_out, Load, QA);
  and and_5 (and_5_out, and_4_out, and_3_out, and_2_out, not_1_out);
  and and_6 (and_6_out, not_4_out, and_1_out);
  and and_7 (and_7_out, not_3_out, and_1_out);
  and and_8 (and_8_out, not_2_out, and_1_out);
  and and_9 (and_9_out, and_4_out, and_3_out, not_2_out);
  and and_10 (and_10_out, not_4_out, and_2_out);
  and and_11 (and_11_out, not_3_out, and_2_out);
  and and_12 (and_12_out, and_4_out, not_3_out);
  and and_13 (and_13_out, not_4_out, and_3_out);
  or or_1 (or_1_out, and_9_out, and_10_out, and_11_out);
  or or_2 (or_2_out, and_12_out, and_13_out);
  or or_3 (or_3_out, and_5_out, and_6_out, and_7_out, and_8_out);
  and and_14 (and_14_out, ~not_5_out, not_4_out);  // And
  and and_15 (and_15_out, or_4_out, Clock);
  and and_16 (and_16_out, Load, Clr, T, P);
  or or_4 (or_4_out, nand_1_out, and_16_out);
  nand nand_1 (nand_1_out, Load, Clr);
  not not_5 (not_5_out, Load);
  and and_17 (and_17_out, not_5_out, D);
  and and_18 (and_18_out, not_5_out, C);
  and and_19 (and_19_out, not_5_out, B);
  and and_20 (and_20_out, not_5_out, A);
  not not_6 (not_6_out, Clr);
  D_FF_AS Z_3_n (.Set(and_17_out), .D(or_3_out), .C(and_15_out), .Clr(not_6_out), .Q(QD));  // open: nQ
  D_FF_AS Z_2_n (.Set(and_18_out), .D(or_1_out), .C(and_15_out), .Clr(not_6_out), .Q(QC));  // open: nQ
  D_FF_AS Z_1_n (.Set(and_19_out), .D(or_2_out), .C(and_15_out), .Clr(not_6_out), .Q(QB));  // open: nQ
  D_FF_AS Z_0_n (.Set(and_20_out), .D(and_14_out), .C(and_15_out), .Clr(not_6_out), .Q(QA));  // open: nQ
  and and_21 (RCO, QD, QC, QB, QA, T);
  // Probe state on {QD, QC, QB, QA}

  // Other names for the same wires on the sheet: Z_0_n = QA; Z_1_n = QB; Z_2_n = QC; Z_3_n = QD
endmodule
