// Digital circuit 01.dig as structural Verilog
module _01 (
  input  P,
  input  T,
  input  D,
  input  C,
  input  B,
  input  A,
  input  Clr,
  input  Load,
  input  Clock,
  output RCO,
  output QD,
  output QC,
  output QB,
  output QA
);

  wire and_2_out, and_3_out, and_4_out, and_5_out, and_6_out, and_7_out, and_8_out, and_9_out, and_10_out,
       and_11_out, and_12_out, and_13_out, and_14_out, and_15_out, and_16_out, and_17_out, multiplexer_1_out,
       multiplexer_2_out, multiplexer_3_out, multiplexer_4_out, not_1_out, not_2_out, not_3_out, not_4_out,
       or_1_out, or_2_out, or_3_out, or_4_out;

  and and_1 (RCO, QA, QB, QC, QD, T);
  // Probe state on {QD, QC, QB, QA}
  not not_1 (not_1_out, QD);
  not not_2 (not_2_out, QC);
  not not_3 (not_3_out, QB);
  not not_4 (not_4_out, QA);
  and and_2 (and_2_out, QA, QB, QC, not_1_out);
  and and_3 (and_3_out, not_4_out, QD);
  and and_4 (and_4_out, not_3_out, QD);
  and and_5 (and_5_out, not_2_out, QD);
  and and_6 (and_6_out, QA, QB, not_2_out);
  and and_7 (and_7_out, not_4_out, QC);
  and and_8 (and_8_out, not_3_out, QC);
  and and_9 (and_9_out, QA, not_3_out);
  and and_10 (and_10_out, not_4_out, QB);
  or or_1 (or_1_out, and_2_out, and_3_out, and_4_out, and_5_out);
  or or_2 (or_2_out, and_6_out, and_7_out, and_8_out);
  or or_3 (or_3_out, and_9_out, and_10_out);
  Multiplexer multiplexer_1 (.sel(Load), .in_0(D), .in_1(or_1_out), .out(multiplexer_1_out));
  Multiplexer multiplexer_2 (.sel(Load), .in_0(C), .in_1(or_2_out), .out(multiplexer_2_out));
  Multiplexer multiplexer_3 (.sel(Load), .in_0(B), .in_1(or_3_out), .out(multiplexer_3_out));
  Multiplexer multiplexer_4 (.sel(Load), .in_0(A), .in_1(not_4_out), .out(multiplexer_4_out));
  and and_11 (and_11_out, Clr, multiplexer_1_out);
  and and_12 (and_12_out, Clr, multiplexer_2_out);
  and and_13 (and_13_out, Clr, multiplexer_3_out);
  and and_14 (and_14_out, Clr, multiplexer_4_out);
  and and_15 (and_15_out, T, P, Load, Clr);
  or or_4 (or_4_out, and_17_out, ~Clr, and_15_out);  // Or
  and and_16 (and_16_out, or_4_out, Clock);
  D_FF Z_3_n (.D(and_11_out), .C(and_16_out), .Q(QD));  // open: nQ
  D_FF Z_2_n (.D(and_12_out), .C(and_16_out), .Q(QC));  // open: nQ
  D_FF Z_1_n (.D(and_13_out), .C(and_16_out), .Q(QB));  // open: nQ
  D_FF Z_0_n (.D(and_14_out), .C(and_16_out), .Q(QA));  // open: nQ
  and and_17 (and_17_out, ~Load, Clr);  // And

  // Other names for the same wires on the sheet: LnD = Load; RST = Clr; Z_0_n = QA; Z_1_n = QB; Z_2_n = QC;
  //   Z_3_n = QD
endmodule
