// Digital circuit 74163-apply.dig as structural Verilog
module _74163_apply (
  input  P,
  input  T,
  input  D,
  input  C,
  input  B,
  input  A,
  input  Clr,
  input  Load,
  input  Clock,
  output QD,
  output QC,
  output QB,
  output QA,
  output RCO
);

  _74163 _74163_1 (
    .pin1(Clr), .pin2(Clock), .pin3(D), .pin4(C), .pin5(B), .pin6(A), .pin7(P), .pin8(1'b0), .pin9(Load),
    .pin10(T), .pin11(QA), .pin12(QB), .pin13(QC), .pin14(QD), .pin15(RCO), .pin16(1'b1));
endmodule
