// Digital circuit 02.dig as structural Verilog
module _02 (
  input  A,
  input  B,
  input  Clr,
  input  Clock,
  output Z
);

  wire add_1_c_o, add_1_s, and_1_out, d_ff_2_q;

  Add add_1 (.a(A), .b(B), .c_i(d_ff_2_q), .s(add_1_s), .c_o(add_1_c_o));
  D_FF d_ff_1 (.D(add_1_s), .C(Clock), .Q(Z));  // open: nQ
  and and_1 (and_1_out, add_1_c_o, Clr);
  D_FF d_ff_2 (.D(and_1_out), .C(Clock), .Q(d_ff_2_q));  // open: nQ
endmodule
