// Digital circuit 03.dig as structural Verilog
module _03 (
  input  P,
  input  Clr,
  input  clock,
  output Z
);

  wire and_1_out, d_ff_1_q, not_1_out, not_2_out;

  not not_1 (not_1_out, Clr);
  and and_1 (and_1_out, P, not_1_out);
  D_FF d_ff_1 (.D(and_1_out), .C(clock), .Q(d_ff_1_q));  // open: nQ
  not not_2 (not_2_out, d_ff_1_q);
  and and_2 (Z, P, not_1_out, not_2_out);
endmodule
