// Digital circuit 09.dig as structural Verilog
module _09 (
  input  P5,
  input  reset,
  input  clock,
  input  P10,
  input  P20,
  input  Pcoffee,
  input  Ptea,
  input  Pchange,
  input  Pnext,
  output [5:0] Balance,
  output CoffeeOut,
  output TeaOut,
  output [1:0] Change5,
  output [1:0] Change10,
  output [1:0] Change20
);

  wire and_8_out, Coffee_Tea, comparator_1_lt, comparator_2_lt, d_ff_1_q, d_ff_2_q, d_ff_3_q, d_ff_4_q,
       d_ff_5_q, d_ff_6_q, d_ff_7_q, multiplexer_1_out, multiplexer_2_out, or_1_out, or_2_out, or_3_out,
       or_4_out, or_5_out, or_6_out, or_7_out, P5_t, P10_t, P20_t, Pchange_t, Pcoffee_t, Pnext_t, Ptea_t;
  wire [2:0] priorityencoder_1_num;
  wire [5:0] add_1_s, add_2_s, BalanceMap_out, div_1_q, div_1_r, div_2_q, div_2_r, div_3_q,
       multiplexer_3_out, multiplexer_4_out, multiplexer_5_out, xor_1_out;
  wire [5:2] d_ff_8_q, d_ff_9_q, d_ff_10_q;

  D_FF d_ff_1 (.D(P5), .C(clock), .Q(d_ff_1_q));  // open: nQ
  D_FF d_ff_2 (.D(P10), .C(clock), .Q(d_ff_2_q));  // open: nQ
  D_FF d_ff_3 (.D(P20), .C(clock), .Q(d_ff_3_q));  // open: nQ
  D_FF d_ff_4 (.D(Pcoffee), .C(clock), .Q(d_ff_4_q));  // open: nQ
  D_FF d_ff_5 (.D(Ptea), .C(clock), .Q(d_ff_5_q));  // open: nQ
  D_FF d_ff_6 (.D(Pchange), .C(clock), .Q(d_ff_6_q));  // open: nQ
  D_FF d_ff_7 (.D(Pnext), .C(clock), .Q(d_ff_7_q));  // open: nQ
  PriorityEncoder #(.Selector_Bits(3)) priorityencoder_1 (
    .in0(Pchange_t), .in1(Ptea_t), .in2(Pcoffee_t), .in3(P20_t), .in4(P10_t), .in5(P5_t), .in6(1'b0),
    .in7(1'b0), .num(priorityencoder_1_num));  // open: any
  and and_1 (P5_t, P5, ~reset, ~d_ff_1_q);  // And
  and and_2 (P10_t, P10, ~reset, ~d_ff_2_q);  // And
  and and_3 (P20_t, P20, ~reset, ~d_ff_3_q);  // And
  and and_4 (Pcoffee_t, Pcoffee, ~reset, ~d_ff_4_q);  // And
  and and_5 (Ptea_t, Ptea, ~reset, ~d_ff_5_q);  // And
  and and_6 (Pchange_t, Pchange, ~reset, ~d_ff_6_q);  // And
  and and_7 (Pnext_t, Pnext, ~reset, ~d_ff_7_q);  // And
  LookUpTable #(.Bits(6)) BalanceMap (
    .in0(priorityencoder_1_num[0]), .in1(priorityencoder_1_num[1]), .in2(priorityencoder_1_num[2]),
    .out(BalanceMap_out));
  Add #(.Bits(6)) add_1 (.a(Balance), .b(BalanceMap_out), .c_i(1'b0), .s(add_1_s));  // open: c_o
  Multiplexer multiplexer_1 (.sel(Coffee_Tea), .in_0(1'b0), .in_1(Pcoffee_t), .out(multiplexer_1_out));
  Multiplexer multiplexer_2 (.sel(Coffee_Tea), .in_0(1'b0), .in_1(Ptea_t), .out(multiplexer_2_out));
  Comparator #(.Bits(6)) comparator_1 (.a(add_1_s), .b(6'b110011), .lt(comparator_1_lt));  // open: gt, eq
  Comparator #(.Bits(6)) comparator_2 (.a(Balance), .b(BalanceMap_out), .lt(comparator_2_lt));  // open: gt, eq
  or or_1 (or_1_out, Ptea_t, Pcoffee_t);
  or or_2 (or_2_out, reset, Pnext_t, Pchange_t);
  or or_3 (or_3_out, reset, Pnext_t, Pchange_t);
  and and_8 (and_8_out, comparator_1_lt, ~Ptea_t, ~Pcoffee_t);  // And
  and and_9 (Coffee_Tea, ~comparator_2_lt, or_1_out);  // And
  JK_FF jk_ff_1 (.J(multiplexer_1_out), .C(clock), .K(or_2_out), .Q(CoffeeOut));  // open: nQ
  JK_FF jk_ff_2 (.J(multiplexer_2_out), .C(clock), .K(or_3_out), .Q(TeaOut));  // open: nQ
  or or_4 (or_4_out, and_8_out, Coffee_Tea);
  or or_5 (or_5_out, CoffeeOut, TeaOut);
  Multiplexer #(.Bits(6)) multiplexer_3 (
    .sel(or_4_out), .in_0({6{1'b0}}), .in_1(BalanceMap_out), .out(multiplexer_3_out));
  Multiplexer #(.Bits(6)) multiplexer_4 (
    .sel(or_5_out), .in_0(multiplexer_3_out), .in_1({6{1'b0}}), .out(multiplexer_4_out));
  or or_6 (or_6_out, Pcoffee_t, Ptea_t);
  Multiplexer #(.Bits(6)) multiplexer_5 (.sel(or_6_out), .in_0({6{1'b0}}), .in_1({6{1'b1}}), .out(multiplexer_5_out));
  assign xor_1_out = multiplexer_5_out ^ multiplexer_4_out;  // XOr xor_1, 6 bits wide
  Add #(.Bits(6)) add_2 (.a(Balance), .b(xor_1_out), .c_i(or_6_out), .s(add_2_s));  // open: c_o
  // Probe on xor_1_out
  Div #(.Bits(6)) div_1 (.a(Balance), .b(6'b010100), .q(div_1_q), .r(div_1_r));
  Div #(.Bits(6)) div_2 (.a(div_1_r), .b(6'b001010), .q(div_2_q), .r(div_2_r));
  Div #(.Bits(6)) div_3 (.a(div_2_r), .b(6'b000101), .q(div_3_q));  // open: r
  or or_7 (or_7_out, reset, Pchange_t);
  D_FF_AS #(.Bits(6)) d_ff_as_1 (.Set(1'b0), .D(add_2_s), .C(clock), .Clr(or_7_out), .Q(Balance));  // open: nQ
  D_FF #(.Bits(6)) d_ff_8 (.D(div_1_q), .C(or_7_out), .Q({d_ff_8_q, Change20}));  // open: nQ
  D_FF #(.Bits(6)) d_ff_9 (.D(div_2_q), .C(or_7_out), .Q({d_ff_9_q, Change10}));  // open: nQ
  D_FF #(.Bits(6)) d_ff_10 (.D(div_3_q), .C(or_7_out), .Q({d_ff_10_q, Change5}));  // open: nQ

  // Notes on the sheet:
  //   contents of BalanceMap (hex, n*v repeats v):
  //   0,14,19,14,a,5
endmodule
