// Digital circuit Lab10.dig as structural Verilog
module Lab10 (
  input  [8:0] N,
  input  reset,
  input  start,
  input  clock,
  output [7:0] displayout,
  output [15:0] clockcount,
  output valid,
  output done
);

  wire and_1_out, and_3_out, and_4_out, and_5_out, and_6_out, and_7_out, comparator_1_gt, comparator_2_eq,
       comparator_4_lt, D0, D1, Displaying, or_2_out, or_3_out, rs_ff_1_q, rs_ff_2_q, Stage0, Stage1;
  wire [7:0] CSum, Max, Mem_d, multiplexer_1_out, multiplexer_3_out, RamAddr, ramdualport_1_d;
  wire [7:7] not_1_out;
  wire [8:0] RomAddr;

  RS_FF rs_ff_1 (.S(start), .C(clock), .R(reset), .Q(rs_ff_1_q));  // open: nQ
  xor xor_1 (Stage0, rs_ff_1_q, D0);
  and and_1 (and_1_out, rs_ff_1_q, D0);
  RS_FF rs_ff_2 (.S(and_1_out), .C(clock), .R(reset), .Q(rs_ff_2_q));  // open: nQ
  xor xor_2 (Stage1, rs_ff_2_q, D1);
  Comparator #(.Bits(8)) comparator_1 (.a(displayout), .b(Max), .gt(comparator_1_gt));  // open: eq, lt
  and and_2 (done, rs_ff_2_q, D1);
  Comparator #(.Bits(8)) comparator_2 (.a({8{1'b1}}), .b(displayout), .eq(comparator_2_eq));  // open: gt, lt
  and and_3 (and_3_out, comparator_2_eq, ~Displaying);  // And
  and and_4 (and_4_out, comparator_1_gt, Stage1);
  or or_1 (D1, and_3_out, and_4_out);
  and and_5 (and_5_out, ~D0, Stage0);  // And
  and and_6 (and_6_out, ~D1, Stage1);  // And
  Seven_Seg_Hex seven_seg_hex_1 (.d(displayout[7:4]), .dp(1'b0));
  Comparator #(.Bits(9)) comparator_3 (.a(RomAddr), .b(N), .eq(D0));  // open: gt, lt
  CounterPreset #(.Bits(9)) Count (
    .en(and_5_out), .C(clock), .dir(1'b0), .in({9{1'b0}}), .ld(1'b0), .clr(reset), .out(RomAddr));  // open: ovf
  CounterPreset #(.Bits(8)) Display (
    .en(and_6_out), .C(clock), .dir(1'b0), .in({8{1'b0}}), .ld(1'b0), .clr(reset), .out(RamAddr));  // open: ovf
  or or_2 (or_2_out, Stage0, Stage1);
  Seven_Seg_Hex seven_seg_hex_2 (.d(displayout[3:0]), .dp(1'b0));
  D_FF d_ff_1 (.D(Displaying), .C(clock), .Q(valid));  // open: nQ
  Counter #(.Bits(16)) counter_1 (.en(or_2_out), .C(clock), .clr(reset), .out(clockcount));  // open: ovf
  ROM #(.AddrBits(9), .isProgramMemory("true"), .Bits(8)) Mem (.A(RomAddr), .sel(Stage0), .D(Mem_d));
  Comparator #(.Bits(8)) comparator_4 (.a(Max), .b(Mem_d), .lt(comparator_4_lt));  // open: gt, eq
  Multiplexer #(.Bits(8)) multiplexer_1 (.sel(Stage0), .in_0({8{1'b0}}), .in_1(Mem_d), .out(multiplexer_1_out));
  Multiplexer #(.Bits(8)) multiplexer_2 (.sel(Stage1), .in_0(multiplexer_1_out), .in_1(RamAddr), .out(displayout));
  and and_7 (and_7_out, comparator_4_lt, Stage0);
  Comparator #(.Bits(8)) comparator_5 (.a({8{1'b0}}), .b(ramdualport_1_d), .lt(Displaying));  // open: gt, eq
  Register #(.Bits(8)) u_Max (.D(Mem_d), .C(clock), .en(and_7_out), .Q(Max));
  // Probe on Max
  or or_3 (or_3_out, Stage0, Stage1);
  RAMDualPort #(.AddrBits(8), .Bits(8)) ramdualport_1 (
    .A(displayout), .Din(CSum), .str(or_3_out), .C(clock), .ld(1'b1), .D(ramdualport_1_d));
  not not_1 (not_1_out[7], D1);
  Multiplexer #(.Bits(8)) multiplexer_3 (
    .sel(Stage1), .in_0({not_1_out[7], {7{1'b0}}}), .in_1({8{1'b1}}), .out(multiplexer_3_out));
  Add #(.Bits(8)) add_1 (.a(ramdualport_1_d), .b(multiplexer_3_out), .c_i(1'b0), .s(CSum));  // open: c_o

  // Other names for the same wires on the sheet: Num[7:0] = displayout

  // Notes on the sheet:
  //   N: default 4
  //   Mem loads t0.bin
endmodule
