// Digital circuit Lab10PushShift.dig as structural Verilog
module Lab10PushShift (
  input  [8:0] N,
  input  reset,
  input  start,
  input  clock,
  output done,
  output [7:0] displayout,
  output [15:0] clockcount,
  output valid
);

  wire comparator_1_gt, not_1_out, Shift;
  wire [7:0] add_1_s, d_ff_1_q, multiplexer_1_out, ramdualaccess_1_d1, ramdualaccess_1_d2, ROMFILE_d;
  wire [8:0] counter_1_out;

  Comparator #(.Bits(9)) comparator_1 (
    .a(counter_1_out), .b(N), .gt(comparator_1_gt), .eq(comparator_1_gt));  // open: lt
  Counter #(.Bits(9)) counter_1 (.en(comparator_1_gt), .C(clock), .clr(1'b0), .out(counter_1_out));  // open: ovf
  ROM #(.AddrBits(9), .isProgramMemory("true"), .Bits(8)) ROMFILE (.A(counter_1_out), .sel(not_1_out), .D(ROMFILE_d));
  not not_1 (not_1_out, Shift);
  Multiplexer #(.Bits(8)) multiplexer_1 (.sel(Shift), .in_0(ROMFILE_d), .in_1(add_1_s), .out(multiplexer_1_out));
  D_FF #(.Bits(8)) d_ff_1 (.D(multiplexer_1_out), .C(clock), .Q(d_ff_1_q));  // open: nQ
  Add #(.Bits(8)) add_1 (.a(d_ff_1_q), .b({8{1'b0}}), .c_i(1'b1), .s(add_1_s));  // open: c_o
  RAMDualAccess #(.AddrBits(8), .isProgramMemory("true"), .Bits(8)) ramdualaccess_1 (
    .str(1'b1), .C(clock), .ld(1'b1), .A1(d_ff_1_q), .Din1(d_ff_1_q), .A2(add_1_s), .D1(ramdualaccess_1_d1),
    .D2(ramdualaccess_1_d2));
  Comparator #(.Bits(8)) comparator_2 (.a(ramdualaccess_1_d1), .b(ramdualaccess_1_d2), .gt(Shift));  // open: eq, lt
  Seven_Seg_Hex seven_seg_hex_1 (.d(4'b0000), .dp(1'b0));
  Seven_Seg_Hex seven_seg_hex_2 (.d(4'b0001), .dp(1'b0));

  assign clockcount = {16{1'b0}};
  assign displayout = 8'h1;
  assign done = 1'b0;
  assign valid = 1'b0;

  // Notes on the sheet:
  //   N: default 4
  //   contents of ROMFILE (hex, n*v repeats v):
  //   9*1,7*0,1,15*0,1,15*0,b,15*0,1,15*0,1
endmodule
