// Digital circuit Lab10Thread.dig as structural Verilog
module Lab10Thread (
  input  [8:0] N,
  input  reset,
  input  start,
  input  clock,
  output [7:0] displayout,
  output [15:0] clockcount,
  output valid,
  output done
);

  wire and_1_out, and_4_out, and_5_out, and_6_out, comparator_2_eq, comparator_3_lt, comparator_4_eq, D0, D1,
       or_1_out, or_2_out, rs_ff_1_q, rs_ff_2_q, Stage0, Stage1;
  wire [7:0] add_1_s, CSum, Max, Mem_d, multiplexer_1_out, multiplexer_3_out, multiplexer_4_out,
       ramdualport_1_d;
  wire [8:0] RomAddr;

  RS_FF rs_ff_1 (.S(start), .C(clock), .R(reset), .Q(rs_ff_1_q));  // open: nQ
  xor xor_1 (Stage0, rs_ff_1_q, D0);
  and and_1 (and_1_out, rs_ff_1_q, D0);
  RS_FF rs_ff_2 (.S(and_1_out), .C(clock), .R(reset), .Q(rs_ff_2_q));  // open: nQ
  xor xor_2 (Stage1, rs_ff_2_q, D1);
  and and_2 (done, rs_ff_2_q, D1);
  and and_3 (D1, D0, comparator_2_eq);
  and and_4 (and_4_out, ~D0, Stage0);  // And
  and and_5 (and_5_out, ~comparator_2_eq, Stage1);  // And
  Seven_Seg_Hex seven_seg_hex_1 (.d(displayout[7:4]), .dp(1'b0));
  Comparator #(.Bits(9)) comparator_1 (.a(RomAddr), .b(N), .eq(D0));  // open: gt, lt
  CounterPreset #(.Bits(9)) Count (
    .en(and_4_out), .C(clock), .dir(1'b0), .in({9{1'b0}}), .ld(1'b0), .clr(reset), .out(RomAddr));  // open: ovf
  Comparator #(.Bits(8)) comparator_2 (.a(displayout), .b(Max), .eq(comparator_2_eq));  // open: gt, lt
  CounterPreset #(.Bits(8)) Display (
    .en(and_5_out), .C(clock), .dir(1'b0), .in({8{1'b0}}), .ld(1'b0), .clr(reset));  // open: out, ovf
  or or_1 (or_1_out, Stage0, Stage1);
  Seven_Seg_Hex seven_seg_hex_2 (.d(displayout[3:0]), .dp(1'b0));
  Counter #(.Bits(16)) counter_1 (.en(or_1_out), .C(clock), .clr(reset), .out(clockcount));  // open: ovf
  ROM #(.AddrBits(9), .Bits(8), .isProgramMemory("true")) Mem (.A(RomAddr), .sel(Stage0), .D(Mem_d));
  Comparator #(.Bits(8)) comparator_3 (.a(Max), .b(Mem_d), .lt(comparator_3_lt));  // open: gt, eq
  Multiplexer #(.Bits(8)) multiplexer_1 (.sel(Stage0), .in_0({8{1'b0}}), .in_1(Mem_d), .out(multiplexer_1_out));
  Multiplexer #(.Bits(8)) multiplexer_2 (.sel(Stage1), .in_0({8{1'b0}}), .in_1(add_1_s), .out(displayout));
  Multiplexer #(.Bits(8)) multiplexer_3 (
    .sel(Stage1), .in_0(multiplexer_1_out), .in_1(add_1_s), .out(multiplexer_3_out));
  Add #(.Bits(8)) add_1 (.a(multiplexer_3_out), .b({8{1'b0}}), .c_i(comparator_4_eq), .s(add_1_s));  // open: c_o
  and and_6 (and_6_out, comparator_3_lt, Stage0);
  Comparator #(.Bits(8)) comparator_4 (
    .a({8{1'b0}}), .b(ramdualport_1_d), .eq(comparator_4_eq), .lt(valid));  // open: gt
  Register #(.Bits(8)) u_Max (.D(Mem_d), .C(clock), .en(and_6_out), .Q(Max));
  // Probe on Max
  or or_2 (or_2_out, Stage0, Stage1);
  RAMDualPort #(.AddrBits(8), .Bits(8)) ramdualport_1 (
    .A(multiplexer_3_out), .Din(CSum), .str(or_2_out), .C(clock), .ld(1'b1), .D(ramdualport_1_d));
  Multiplexer #(.Bits(8)) multiplexer_4 (.sel(Stage1), .in_0(8'h1), .in_1({8{1'b1}}), .out(multiplexer_4_out));
  Add #(.Bits(8)) add_2 (.a(ramdualport_1_d), .b(multiplexer_4_out), .c_i(1'b0), .s(CSum));  // open: c_o

  // Other names for the same wires on the sheet: Displaying = valid; Num[7:0] = displayout

  // Notes on the sheet:
  //   N: default 3
  //   Stager
  //   Mem loads test.bin
endmodule
