// Digital circuit MiniSorter.dig as structural Verilog
module MiniSorter (
  input  A,
  input  B,
  output A_2,
  output B_2
);

  wire comparator_1_gt, comparator_1_lt;

  Multiplexer multiplexer_1 (.sel(comparator_1_gt), .in_0(A), .in_1(B), .out(A_2));
  Comparator comparator_1 (.a(A), .b(B), .gt(comparator_1_gt), .lt(comparator_1_lt));  // open: eq
  Multiplexer multiplexer_2 (.sel(comparator_1_lt), .in_0(B), .in_1(A), .out(B_2));
endmodule
