// Digital circuit 10to165.dig as structural Verilog
module _10to165 (
  input  clk,
  input  RST,
  output [7:0] out_2
);

  wire _74163_1_pin9, _74163_1_pin15, and_1_out, d_ff_1_q, or_1_out, or_2_out, rs_ff_as_1_nq;

  _74163 _74163_1 (
    .pin1(1'b1), .pin2(clk), .pin3(1'b0), .pin4(1'b1), .pin5(1'b0), .pin6(1'b1), .pin7(1'b1), .pin8(1'b0),
    .pin9(_74163_1_pin9), .pin10(1'b1), .pin11(out_2[3]), .pin12(out_2[2]), .pin13(out_2[1]),
    .pin14(out_2[0]), .pin15(_74163_1_pin15), .pin16(1'b1));
  or or_1 (or_1_out, or_2_out, _74163_1_pin15);
  D_FF d_ff_1 (.D(or_1_out), .C(clk), .Q(d_ff_1_q));  // open: nQ
  and and_1 (and_1_out, ~out_2[4], out_2[5], ~out_2[6], out_2[7], out_2[0], ~out_2[1], out_2[2], ~out_2[3]);  // And
  _74163 _74163_2 (
    .pin1(1'b1), .pin2(d_ff_1_q), .pin3(1'b0), .pin4(1'b0), .pin5(1'b0), .pin6(1'b0), .pin7(1'b1),
    .pin8(1'b0), .pin9(_74163_1_pin9), .pin10(1'b1), .pin11(out_2[7]), .pin12(out_2[6]), .pin13(out_2[5]),
    .pin14(out_2[4]), .pin16(1'b1));  // open: pin15
  RS_FF_AS rs_ff_as_1 (.S(clk), .R(1'b0), .nQ(rs_ff_as_1_nq));  // open: Q
  or or_2 (or_2_out, and_1_out, rs_ff_as_1_nq, RST);
  not not_1 (_74163_1_pin9, or_2_out);
endmodule
